// Logisim project digital clock.circ as structural Verilog: 7 circuits, main circuit user_interface
module user_interface (
  input  turn_on_off,
  input  display_alarm,
  input  enable,
  input  switch,
  input  run,
  input  u_d,
  input  display_timer
);

  wire combination_1_fri, combination_1_mon, combination_1_out_15, combination_1_out_16,
       combination_1_out_17, combination_1_out_18, combination_1_out_19, combination_1_out_20,
       combination_1_out_21, combination_1_out_22, combination_1_out_23, combination_1_out_24,
       combination_1_out_25, combination_1_out_26, combination_1_out_27, combination_1_out_28,
       combination_1_out_29, combination_1_out_30, combination_1_out_31, combination_1_out_32,
       combination_1_out_33, combination_1_out_34, combination_1_out_35, combination_1_out_36,
       combination_1_out_37, combination_1_out_38, combination_1_out_39, combination_1_out_40,
       combination_1_out_41, combination_1_out_42, combination_1_out_43, combination_1_out_44,
       combination_1_out_45, combination_1_out_46, combination_1_out_47, combination_1_out_48,
       combination_1_out_49, combination_1_out_50, combination_1_out_51, combination_1_out_52,
       combination_1_out_53, combination_1_out_54, combination_1_out_55, combination_1_out_56,
       combination_1_out_57, combination_1_out_58, combination_1_out_59, combination_1_sat,
       combination_1_sun, combination_1_thr, combination_1_tue, combination_1_wed, hours_out, minutes_out,
       R_out, RA_out, RT_out, seconds_out, Weekdays_out;

  LED led_1 (.in(combination_1_out_57));
  LED led_2 (.in(combination_1_out_58));
  Button R (.out(R_out));
  Button Weekdays (.out(Weekdays_out));
  LED MON (.in(combination_1_mon));
  _7_Segment_Display u_7_segment_display_1 (
    .g(combination_1_out_15), .f(combination_1_out_16), .a(combination_1_out_17), .b(combination_1_out_18),
    .e(combination_1_out_39), .d(combination_1_out_40), .c(combination_1_out_41));  // open: dp
  combination combination_1 (
    .in_12(hours_out), .in_6(Weekdays_out), .in_7(turn_on_off), .in_13(minutes_out), .in_2(switch),
    .in_14(seconds_out), .in_11(enable), .in_8(RA_out), .in_9(display_alarm), .in_10(R_out),
    .in_1(display_timer), .in_3(u_d), .in_4(RT_out), .in_5(run), .out_39(combination_1_out_39),
    .out_15(combination_1_out_15), .out_40(combination_1_out_40), .out_16(combination_1_out_16),
    .out_41(combination_1_out_41), .out_17(combination_1_out_17), .out_18(combination_1_out_18),
    .mon(combination_1_mon), .tue(combination_1_tue), .wed(combination_1_wed), .thr(combination_1_thr),
    .fri(combination_1_fri), .SAT(combination_1_sat), .sun(combination_1_sun), .out_42(combination_1_out_42),
    .out_19(combination_1_out_19), .out_43(combination_1_out_43), .out_20(combination_1_out_20),
    .out_44(combination_1_out_44), .out_21(combination_1_out_21), .out_22(combination_1_out_22),
    .out_45(combination_1_out_45), .out_23(combination_1_out_23), .out_46(combination_1_out_46),
    .out_24(combination_1_out_24), .out_47(combination_1_out_47), .out_25(combination_1_out_25),
    .out_26(combination_1_out_26), .out_59(combination_1_out_59), .out_48(combination_1_out_48),
    .out_27(combination_1_out_27), .out_49(combination_1_out_49), .out_28(combination_1_out_28),
    .out_50(combination_1_out_50), .out_29(combination_1_out_29), .out_30(combination_1_out_30),
    .out_51(combination_1_out_51), .out_31(combination_1_out_31), .out_52(combination_1_out_52),
    .out_32(combination_1_out_32), .out_53(combination_1_out_53), .out_33(combination_1_out_33),
    .out_34(combination_1_out_34), .out_54(combination_1_out_54), .out_35(combination_1_out_35),
    .out_55(combination_1_out_55), .out_36(combination_1_out_36), .out_56(combination_1_out_56),
    .out_37(combination_1_out_37), .out_38(combination_1_out_38), .out_57(combination_1_out_57),
    .out_58(combination_1_out_58));
  LED TUE (.in(combination_1_tue));
  LED WED (.in(combination_1_wed));
  _7_Segment_Display u_7_segment_display_2 (
    .g(combination_1_out_19), .f(combination_1_out_20), .a(combination_1_out_21), .b(combination_1_out_22),
    .e(combination_1_out_42), .d(combination_1_out_43), .c(combination_1_out_44));  // open: dp
  _7_Segment_Display u_7_segment_display_3 (
    .g(combination_1_out_23), .f(combination_1_out_24), .a(combination_1_out_25), .b(combination_1_out_26),
    .e(combination_1_out_45), .d(combination_1_out_46), .c(combination_1_out_47));  // open: dp
  LED THUR (.in(combination_1_thr));
  LED FRI (.in(combination_1_fri));
  _7_Segment_Display u_7_segment_display_4 (
    .g(combination_1_out_27), .f(combination_1_out_28), .a(combination_1_out_29), .b(combination_1_out_30),
    .e(combination_1_out_48), .d(combination_1_out_49), .c(combination_1_out_50));  // open: dp
  LED SAT (.in(combination_1_sat));
  LED SUN (.in(combination_1_sun));
  _7_Segment_Display u_7_segment_display_5 (
    .g(combination_1_out_31), .f(combination_1_out_32), .a(combination_1_out_33), .b(combination_1_out_34),
    .e(combination_1_out_51), .d(combination_1_out_52), .c(combination_1_out_53));  // open: dp
  _7_Segment_Display u_7_segment_display_6 (
    .g(combination_1_out_35), .f(combination_1_out_36), .a(combination_1_out_37), .b(combination_1_out_38),
    .e(combination_1_out_54), .d(combination_1_out_55), .c(combination_1_out_56));  // open: dp
  Button RT (.out(RT_out));
  LED led_3 (.in(combination_1_out_59));
  Button RA (.out(RA_out));
  Button hours (.out(hours_out));
  Button minutes (.out(minutes_out));
  Button seconds (.out(seconds_out));

  // Notes on the sheet:
  //   IVA SEKULIC 21309706
  //   adjust weekdays manually using this button
  //   Reset the clock
  //   Start the clock
  //   Objective: Design a clock with an alarm system, timer and stopwatch
  //   Have the time running whilst using different features
  //   Use the least amount of flipflops and logic gates
  //   Switch to 12 hour time and AM/PM will light up
  //   Weekdays
  //   Make sure to reset the alarm if using again
  //   Make sure to turn on the alarm once desired time has been set
  //   u_d = logic low to count up; logic high to count down
  //   NOTE: do not have display_alarm and display_timer on at the same time
  //   Once you set your time with buttons you can count down by pressing u_d and then pressing run
endmodule

module combination (
  input  in_1,
  input  in_2,
  input  in_3,
  input  in_4,
  input  in_5,
  input  in_6,
  input  in_7,
  input  in_8,
  input  in_9,
  input  in_10,
  input  in_11,
  input  in_12,
  input  in_13,
  input  in_14,
  output out_15,
  output out_16,
  output out_17,
  output out_18,
  output out_19,
  output out_20,
  output out_21,
  output out_22,
  output out_23,
  output out_24,
  output out_25,
  output out_26,
  output out_27,
  output out_28,
  output out_29,
  output out_30,
  output out_31,
  output out_32,
  output out_33,
  output out_34,
  output out_35,
  output out_36,
  output out_37,
  output out_38,
  output out_39,
  output out_40,
  output out_41,
  output out_42,
  output out_43,
  output out_44,
  output out_45,
  output out_46,
  output out_47,
  output out_48,
  output out_49,
  output out_50,
  output out_51,
  output out_52,
  output out_53,
  output out_54,
  output out_55,
  output out_56,
  output out_57,
  output out_58,
  output out_59,
  output mon,
  output tue,
  output wed,
  output thr,
  output fri,
  output SAT,
  output sun
);

  wire alarm_clock_1_am, alarm_clock_1_pm, clock_1_out, demultiplexer_1_out0, demultiplexer_1_out1,
       demultiplexer_2_out0, demultiplexer_2_out1, demultiplexer_3_out0, demultiplexer_3_out1;
  wire [2:0] alarm_clock_1_wekdayout;
  wire [3:0] alarm_clock_1_hour1, alarm_clock_1_hour2, alarm_clock_1_out_15, alarm_clock_1_out_16,
       alarm_clock_1_out_17, alarm_clock_1_out_18, alarm_clock_1_out_19, alarm_clock_1_out_20,
       bcd_to_7_segment_decoder_1_p5, bcd_to_7_segment_decoder_2_p6, bcd_to_7_segment_decoder_3_p5,
       bcd_to_7_segment_decoder_4_p6, bcd_to_7_segment_decoder_5_p5, bcd_to_7_segment_decoder_6_p6,
       count_1_out_9, count_1_out_10, count_1_out_11, count_1_out_12, count_1_out_13, count_1_out_14,
       multiplexer_1_out, multiplexer_2_out;

  // BCD_to_7_Segment_decoder bcd_to_7_segment_decoder_1: pin names not known; wires that end beside it: out_15, out_39, out_16, out_40, bcd_to_7_segment_decoder_1_p5, out_17, out_41
  Multiplexer #(.width(4)) multiplexer_1 (
    .in0(alarm_clock_1_out_17), .in1(alarm_clock_1_hour1), .out(multiplexer_1_out), .sel(in_2));
  // BCD_to_7_Segment_decoder bcd_to_7_segment_decoder_2: pin names not known; wires that end beside it: out_18, out_19, out_42, out_20, out_43, bcd_to_7_segment_decoder_2_p6, out_21, out_44, out_22
  // BCD_to_7_Segment_decoder bcd_to_7_segment_decoder_3: pin names not known; wires that end beside it: out_23, out_45, out_24, out_46, bcd_to_7_segment_decoder_3_p5, out_25, out_47
  Multiplexer #(.width(4)) multiplexer_2 (
    .in0(alarm_clock_1_out_19), .in1(alarm_clock_1_hour2), .out(multiplexer_2_out), .sel(in_2));
  Decoder #(.select(3)) decoder_1 (
    .out0(mon), .out1(tue), .out2(wed), .out3(thr), .out4(fri), .out5(SAT), .out6(sun),
    .sel(alarm_clock_1_wekdayout), .en(1'b1));  // open: out7
  Demultiplexer demultiplexer_1 (.out0(demultiplexer_1_out0), .out1(demultiplexer_1_out1), .in(in_12), .sel(in_9));
  // BCD_to_7_Segment_decoder bcd_to_7_segment_decoder_4: pin names not known; wires that end beside it: out_26, out_27, out_48, out_28, out_49, bcd_to_7_segment_decoder_4_p6, out_29, out_50, out_30
  alarm_clock alarm_clock_1 (
    .bahr(demultiplexer_1_out1), .bamin(demultiplexer_2_out1), .reset(in_10), .weekdayinput(in_6),
    .clck(clock_1_out), .basec(demultiplexer_3_out1), .turnoff(in_7), .enable12(in_11), .enable(in_11),
    .reset_alarm(in_8), .enable_alarm(in_9), .out_17(alarm_clock_1_out_17), .PM(alarm_clock_1_pm),
    .AM(alarm_clock_1_am), .out_19(alarm_clock_1_out_19), .out_15(alarm_clock_1_out_15),
    .out_18(alarm_clock_1_out_18), .out_16(alarm_clock_1_out_16), .out_20(alarm_clock_1_out_20),
    .wekdayout(alarm_clock_1_wekdayout), .led(out_59), .hour1(alarm_clock_1_hour1),
    .hour2(alarm_clock_1_hour2));
  Demultiplexer demultiplexer_2 (.out0(demultiplexer_2_out0), .out1(demultiplexer_2_out1), .in(in_13), .sel(in_9));
  Demultiplexer demultiplexer_3 (.out0(demultiplexer_3_out0), .out1(demultiplexer_3_out1), .in(in_14), .sel(in_9));
  // BCD_to_7_Segment_decoder bcd_to_7_segment_decoder_5: pin names not known; wires that end beside it: out_31, out_51, out_32, out_52, bcd_to_7_segment_decoder_5_p5, out_33, out_53
  // BCD_to_7_Segment_decoder bcd_to_7_segment_decoder_6: pin names not known; wires that end beside it: out_34, out_35, out_54, out_36, out_55, bcd_to_7_segment_decoder_6_p6, out_37, out_56, out_38
  Clock clock_1 (.out(clock_1_out));
  Multiplexer #(.width(4)) multiplexer_3 (
    .in0(alarm_clock_1_out_20), .in1(count_1_out_12), .out(bcd_to_7_segment_decoder_6_p6), .sel(in_1));
  Multiplexer #(.width(4)) multiplexer_4 (
    .in0(alarm_clock_1_out_16), .in1(count_1_out_11), .out(bcd_to_7_segment_decoder_5_p5), .sel(in_1));
  Multiplexer #(.width(4)) multiplexer_5 (
    .in0(alarm_clock_1_out_18), .in1(count_1_out_9), .out(bcd_to_7_segment_decoder_4_p6), .sel(in_1));
  Multiplexer #(.width(4)) multiplexer_6 (
    .in0(alarm_clock_1_out_15), .in1(count_1_out_10), .out(bcd_to_7_segment_decoder_3_p5), .sel(in_1));
  Multiplexer #(.width(4)) multiplexer_7 (
    .in0(multiplexer_2_out), .in1(count_1_out_13), .out(bcd_to_7_segment_decoder_2_p6), .sel(in_1));
  Multiplexer #(.width(4)) multiplexer_8 (
    .in0(multiplexer_1_out), .in1(count_1_out_14), .out(bcd_to_7_segment_decoder_1_p5), .sel(in_1));
  and and_1 (out_57, in_2, alarm_clock_1_am);
  and and_2 (out_58, alarm_clock_1_pm, in_2);
  count count_1 (
    .bmin(demultiplexer_2_out0), .bsec(demultiplexer_3_out0), .clck(clock_1_out), .up_down(in_3),
    .enable(1'b1), .reset(in_4), .run(in_5), .bhr(demultiplexer_1_out0), .out_9(count_1_out_9),
    .out_11(count_1_out_11), .out_12(count_1_out_12), .out_14(count_1_out_14), .out_13(count_1_out_13),
    .out_10(count_1_out_10));

  // Other names for the same wires on the sheet: l = in_2

  // Notes on the sheet:
  //   Weekday Decoder
  //   All of the circuits needed to design this clock are placed in one subcircuit
  //   We use multiplexers in order to allow the user to switch between clock, alarm and timer displays
endmodule

module mod10 (
  input  up0,
  input  enable,
  input  reset,
  input  button,
  input  run,
  input  a1,
  input  b1,
  input  reset_alarm,
  input  enable_alarm,
  input  buttonA,
  output [3:0] output1,
  output a,
  output b,
  output a10,
  output [3:0] display,
  output overflow_alarm
);

  wire a1_t, and_1_out, and_2_out, and_3_out, and_4_out, and_6_out, b1_t, c1, d1, not_1_out, not_2_out,
       or_1_out, or_2_out, or_3_out, or_4_out, or_5_out, or_6_out, t_ff_1_qn, t_ff_2_qn, t_ff_3_qn,
       xor_1_out, xor_2_out, xor_3_out, xor_4_out;
  wire [3:0] adder_1_out, demultiplexer_1_out0, demultiplexer_1_out1, multiplexer_2_out, subtractor_1_out;

  and and_1 (and_1_out, run, or_1_out);
  or or_1 (or_1_out, a1, b1);
  D_Flip_Flop d_ff_1 (.D(and_2_out), .clk(or_2_out), .Q(output1[0]), .reset(or_3_out));  // open: Qn, preset
  and and_2 (and_2_out, multiplexer_2_out[0], enable);
  or or_2 (or_2_out, and_1_out, button);
  or or_3 (or_3_out, a, reset);
  D_Flip_Flop d_ff_2 (.D(and_3_out), .clk(or_2_out), .Q(output1[1]), .reset(or_4_out));  // open: Qn, preset
  and and_3 (and_3_out, multiplexer_2_out[1], enable);
  or or_4 (or_4_out, a, reset, b);
  T_Flip_Flop t_ff_1 (.T(enable_alarm), .clk(buttonA), .Q(a1_t), .Qn(t_ff_1_qn), .reset(or_6_out));  // open: preset
  Multiplexer #(.width(4)) multiplexer_1 (.in0(output1), .in1({d1, c1, b1_t, a1_t}), .out(display), .sel(enable_alarm));
  T_Flip_Flop t_ff_2 (.T(enable_alarm), .clk(t_ff_1_qn), .Q(b1_t), .Qn(t_ff_2_qn), .reset(or_6_out));  // open: preset
  Adder #(.width(4)) adder_1 (.a(output1), .b(4'b0001), .out(adder_1_out));  // open: cin, cout
  Subtractor #(.width(4)) subtractor_1 (.a(output1), .b(4'b0001), .out(subtractor_1_out));  // open: bin, bout
  D_Flip_Flop d_ff_3 (.D(and_4_out), .clk(or_2_out), .Q(output1[2]), .reset(or_5_out));  // open: Qn, preset
  and and_4 (and_4_out, multiplexer_2_out[2], enable);
  Multiplexer #(.width(4)) multiplexer_2 (
    .in0(adder_1_out), .in1(subtractor_1_out), .out(multiplexer_2_out), .sel(up0));
  or or_5 (or_5_out, a, reset, b);
  T_Flip_Flop t_ff_3 (.T(enable_alarm), .clk(t_ff_2_qn), .Q(c1), .Qn(t_ff_3_qn), .reset(or_6_out));  // open: preset
  Demultiplexer #(.width(4)) demultiplexer_1 (
    .out0(demultiplexer_1_out0), .out1(demultiplexer_1_out1), .in(output1), .sel(up0));
  and and_5 (b, demultiplexer_1_out1[2], demultiplexer_1_out1[3], demultiplexer_1_out1[1], demultiplexer_1_out1[0]);
  T_Flip_Flop t_ff_4 (.T(enable_alarm), .clk(t_ff_3_qn), .Q(d1), .reset(or_6_out));  // open: Qn, preset
  D_Flip_Flop d_ff_4 (.D(and_6_out), .clk(or_2_out), .Q(output1[3]), .reset(a));  // open: Qn, preset
  and and_6 (and_6_out, multiplexer_2_out[3], enable);
  and and_7 (overflow_alarm, b1_t, d1);
  or or_6 (or_6_out, overflow_alarm, reset_alarm);
  not not_1 (not_1_out, demultiplexer_1_out0[2]);
  and and_8 (a, demultiplexer_1_out0[3], not_1_out, not_2_out, demultiplexer_1_out0[1]);
  not not_2 (not_2_out, demultiplexer_1_out0[0]);
  xor xor_1 (xor_1_out, d1, output1[3]);
  xor xor_2 (xor_2_out, c1, output1[2]);
  xor xor_3 (xor_3_out, b1_t, output1[1]);
  xor xor_4 (xor_4_out, a1_t, output1[0]);
  nor nor_1 (a10, xor_1_out, xor_2_out, xor_3_out, xor_4_out);

  // Other names for the same wires on the sheet: a_t = output1[0]; b_t = output1[1]; c = output1[2]; d = output1[3]

  // Notes on the sheet:
  //   This is the count up/down mod10 counter
  //   The alarm couner
  //   run is needed in order to be able to adjust the timer with buttons without the clock interfering 
  //   A logic high output produced when all of the mod10 counter digits are same as the alarm one
endmodule

module mod6 (
  input  up0,
  input  enable,
  input  reset,
  input  run,
  input  a1,
  input  b1,
  input  reset_alarm,
  input  enable_alarm,
  input  button,
  output [3:0] output2,
  output a,
  output b,
  output a6,
  output [3:0] display
);

  wire a1_t, and_1_out, and_2_out, and_3_out, and_4_out, and_7_out, b1_t, c1, not_1_out, or_1_out, or_2_out,
       or_3_out, or_4_out, or_5_out, t_ff_1_qn, t_ff_2_qn, xor_1_out, xor_2_out, xor_3_out;
  wire [3:0] adder_1_out, demultiplexer_1_out0, demultiplexer_1_out1, multiplexer_2_out, subtractor_1_out;

  and and_1 (and_1_out, run, or_1_out);
  or or_1 (or_1_out, a1, b1);
  D_Flip_Flop d_ff_1 (.D(and_2_out), .clk(and_1_out), .Q(output2[0]), .reset(or_2_out));  // open: Qn, preset
  and and_2 (and_2_out, multiplexer_2_out[0], enable);
  or or_2 (or_2_out, a, reset);
  D_Flip_Flop d_ff_2 (.D(and_3_out), .clk(and_1_out), .Q(output2[1]), .reset(or_3_out));  // open: Qn, preset
  and and_3 (and_3_out, multiplexer_2_out[1], enable);
  or or_3 (or_3_out, b, reset, a);
  T_Flip_Flop t_ff_1 (.T(enable_alarm), .clk(button), .Q(a1_t), .Qn(t_ff_1_qn), .reset(or_5_out));  // open: preset
  Adder #(.width(4)) adder_1 (.a({1'b0, output2[2:0]}), .b(4'b0001), .out(adder_1_out));  // open: cin, cout
  Subtractor #(.width(4)) subtractor_1 (
    .a({1'b0, output2[2:0]}), .b(4'b0001), .out(subtractor_1_out));  // open: bin, bout
  Multiplexer #(.width(4)) multiplexer_1 (
    .in0({1'b0, output2[2:0]}), .in1({1'b0, c1, b1_t, a1_t}), .out(display), .sel(enable_alarm));
  T_Flip_Flop t_ff_2 (.T(enable_alarm), .clk(t_ff_1_qn), .Q(b1_t), .Qn(t_ff_2_qn), .reset(or_5_out));  // open: preset
  Multiplexer #(.width(4)) multiplexer_2 (
    .in0(adder_1_out), .in1(subtractor_1_out), .out(multiplexer_2_out), .sel(up0));
  D_Flip_Flop d_ff_3 (.D(and_4_out), .clk(and_1_out), .Q(output2[2]), .reset(or_4_out));  // open: Qn, preset
  and and_4 (and_4_out, multiplexer_2_out[2], enable);
  or or_4 (or_4_out, a, reset);
  T_Flip_Flop t_ff_3 (.T(enable_alarm), .clk(t_ff_2_qn), .Q(c1), .reset(or_5_out));  // open: Qn, preset
  Demultiplexer #(.width(4)) demultiplexer_1 (
    .out0(demultiplexer_1_out0), .out1(demultiplexer_1_out1), .in({1'b0, output2[2:0]}), .sel(up0));
  and and_5 (b, demultiplexer_1_out1[2], demultiplexer_1_out1[1], demultiplexer_1_out1[0]);
  and and_6 (a, demultiplexer_1_out0[2], demultiplexer_1_out0[1], not_1_out);
  and and_7 (and_7_out, b1_t, c1);
  or or_5 (or_5_out, and_7_out, reset_alarm);
  not not_1 (not_1_out, demultiplexer_1_out0[0]);
  xor xor_1 (xor_1_out, c1, output2[2]);
  xor xor_2 (xor_2_out, b1_t, output2[1]);
  xor xor_3 (xor_3_out, a1_t, output2[0]);
  nor nor_1 (a6, 1'b0, xor_1_out, xor_2_out, xor_3_out);

  assign output2[3] = 1'b0;

  // Other names for the same wires on the sheet: a_t = output2[0]; b_t = output2[1]; c = output2[2]
endmodule

module mod3 (
  input  up0,
  input  enable,
  input  reset,
  input  run,
  input  a1,
  input  b1,
  input  reset_alarm,
  input  enable_alarm,
  input  button,
  output [3:0] output3,
  output a,
  output b,
  output a3,
  output [3:0] display
);

  wire a1_t, and_1_out, and_2_out, and_3_out, and_5_out, b1_t, or_1_out, or_2_out, or_3_out, or_4_out,
       t_ff_1_qn, xor_1_out, xor_2_out;
  wire [3:0] adder_1_out, demultiplexer_1_out0, demultiplexer_1_out1, multiplexer_2_out, subtractor_1_out;

  and and_1 (and_1_out, run, or_1_out);
  or or_1 (or_1_out, a1, b1);
  D_Flip_Flop d_ff_1 (.D(and_2_out), .clk(and_1_out), .Q(output3[0]), .reset(or_2_out));  // open: Qn, preset
  and and_2 (and_2_out, multiplexer_2_out[0], enable);
  or or_2 (or_2_out, a, reset, b);
  T_Flip_Flop t_ff_1 (.T(enable_alarm), .clk(button), .Q(a1_t), .Qn(t_ff_1_qn), .reset(or_4_out));  // open: preset
  D_Flip_Flop d_ff_2 (.D(and_3_out), .clk(and_1_out), .Q(output3[1]), .reset(or_3_out));  // open: Qn, preset
  and and_3 (and_3_out, multiplexer_2_out[1], enable);
  or or_3 (or_3_out, a, reset);
  Multiplexer #(.width(4)) multiplexer_1 (
    .in0({2'b00, output3[1:0]}), .in1({2'b00, b1_t, a1_t}), .out(display), .sel(enable_alarm));
  T_Flip_Flop t_ff_2 (.T(enable_alarm), .clk(t_ff_1_qn), .Q(b1_t), .reset(or_4_out));  // open: Qn, preset
  Adder #(.width(4)) adder_1 (.a({2'b00, output3[1:0]}), .b(4'b0001), .out(adder_1_out));  // open: cin, cout
  Subtractor #(.width(4)) subtractor_1 (
    .a({2'b00, output3[1:0]}), .b(4'b0001), .out(subtractor_1_out));  // open: bin, bout
  Multiplexer #(.width(4)) multiplexer_2 (
    .in0(adder_1_out), .in1(subtractor_1_out), .out(multiplexer_2_out), .sel(up0));
  Demultiplexer #(.width(4)) demultiplexer_1 (
    .out0(demultiplexer_1_out0), .out1(demultiplexer_1_out1), .in({2'b00, output3[1:0]}), .sel(up0));
  and and_4 (b, demultiplexer_1_out1[1], demultiplexer_1_out1[0]);
  and and_5 (and_5_out, b1_t, a1_t);
  or or_4 (or_4_out, and_5_out, reset_alarm);
  and and_6 (a, demultiplexer_1_out0[1], demultiplexer_1_out0[0]);
  xor xor_1 (xor_1_out, b1_t, output3[1]);
  xor xor_2 (xor_2_out, a1_t, output3[0]);
  nor nor_1 (a3, 1'b0, 1'b0, xor_1_out, xor_2_out);

  assign output3[3:2] = 2'b00;

  // Other names for the same wires on the sheet: a_t = output3[0]; b_t = output3[1]
endmodule

module alarm_clock (
  input  turnoff,
  input  bahr,
  input  bamin,
  input  clck,
  input  basec,
  input  enable12,
  input  enable,
  input  reset_alarm,
  input  enable_alarm,
  input  weekdayinput,
  input  reset,
  output led,
  output [3:0] hour1,
  output [3:0] hour2,
  output [3:0] out_15,
  output [3:0] out_16,
  output [3:0] out_17,
  output [3:0] out_18,
  output [3:0] out_19,
  output [3:0] out_20,
  output [2:0] wekdayout,
  output AM,
  output PM
);

  wire and_1_out, and_2_out, and_3_out, and_4_out, and_5_out, and_6_out, and_7_out, and_8_out, and_9_out,
       and_10_out, clock_1_out, clock_2_out, d_ff_1_qn, mod3_2_a3, mod6_1_a, mod6_1_a6, mod6_2_a, mod6_2_a6,
       mod10_1_a, mod10_2_a, mod10_2_a10, mod10_2_overflow_alarm, mod10_3_a, mod10_3_a10,
       mod10_3_overflow_alarm, mod10_4_a, mod10_4_a10, mod10_4_overflow_alarm, nor_1_out, nor_2_out,
       not_1_out, not_2_out, not_3_out, not_4_out, not_5_out, not_6_out, not_7_out, not_8_out, not_9_out,
       not_11_out, not_12_out, not_13_out, or_1_out, or_2_out, or_3_out, or_4_out, t_ff_1_qn, t_ff_2_qn,
       t_ff_4_q, t_ff_5_q;
  wire [3:0] mod3_1_display, mod10_1_display;

  mod3 mod3_1 (
    .enable(enable12), .reset(or_2_out), .a1(mod10_1_a), .display(mod3_1_display));  // open: up0, run, b1, reset_alarm, enable_alarm, button, output3, a, b, a3
  nor nor_1 (nor_1_out, mod3_1_display[0], mod3_1_display[1], mod3_1_display[2], mod3_1_display[3]);
  and and_1 (and_1_out, nor_1_out, nor_2_out);
  nor nor_2 (nor_2_out, mod10_1_display[0], mod10_1_display[1], mod10_1_display[2], mod10_1_display[3]);
  mod10 mod10_1 (
    .enable(enable12), .reset(or_2_out), .a1(mod10_2_a), .a(mod10_1_a), .display(mod10_1_display));  // open: up0, button, run, b1, reset_alarm, enable_alarm, buttonA, output1, b, a10, overflow_alarm
  not not_1 (not_1_out, mod3_1_display[1]);
  not not_2 (not_2_out, mod3_1_display[2]);
  not not_3 (not_3_out, mod3_1_display[3]);
  and and_2 (and_2_out, not_1_out, mod3_1_display[0], not_2_out, not_3_out);
  Multiplexer #(.width(4)) multiplexer_1 (.in0(mod3_1_display), .in1(4'b0001), .out(hour1), .sel(and_1_out));
  Multiplexer #(.width(4)) multiplexer_2 (.in0(mod10_1_display), .in1(4'b0010), .out(hour2), .sel(and_1_out));
  not not_4 (not_4_out, mod10_1_display[0]);
  not not_5 (not_5_out, mod10_1_display[2]);
  not not_6 (not_6_out, mod10_1_display[3]);
  mod3 mod3_2 (
    .enable(enable), .reset(or_3_out), .run(enable), .a1(mod10_2_a), .reset_alarm(reset_alarm),
    .enable_alarm(enable_alarm), .button(mod10_2_overflow_alarm), .a3(mod3_2_a3), .display(out_17));  // open: up0, b1, output3, a, b
  and and_3 (and_3_out, mod10_1_display[1], not_4_out, not_5_out, not_6_out);
  and and_4 (and_4_out, and_3_out, and_2_out);
  and and_5 (and_5_out, reset, PM);
  or or_1 (or_1_out, and_4_out, and_5_out);
  mod10 mod10_2 (
    .enable(enable), .reset(or_3_out), .run(enable), .a1(mod6_1_a), .reset_alarm(reset_alarm),
    .enable_alarm(enable_alarm), .buttonA(bahr), .a(mod10_2_a), .a10(mod10_2_a10), .display(out_19),
    .overflow_alarm(mod10_2_overflow_alarm));  // open: up0, button, b1, output1, b
  not not_7 (not_7_out, out_17[0]);
  not not_8 (not_8_out, out_17[2]);
  not not_9 (not_9_out, out_17[3]);
  D_Flip_Flop d_ff_1 (.D(d_ff_1_qn), .clk(or_1_out), .Q(PM), .Qn(d_ff_1_qn));  // open: preset, reset
  and and_6 (and_6_out, not_7_out, out_17[1], not_8_out, not_9_out);
  not not_10 (AM, PM);
  mod6 mod6_1 (
    .enable(enable), .reset(or_3_out), .run(enable), .a1(mod10_3_a), .reset_alarm(reset_alarm),
    .enable_alarm(enable_alarm), .button(mod10_3_overflow_alarm), .a(mod6_1_a), .a6(mod6_1_a6),
    .display(out_15));  // open: up0, b1, output2, b
  not not_11 (not_11_out, out_19[0]);
  not not_12 (not_12_out, out_19[1]);
  not not_13 (not_13_out, out_19[3]);
  and and_7 (and_7_out, not_11_out, not_12_out, out_19[2], not_13_out);
  or or_2 (or_2_out, and_4_out, reset);
  mod10 mod10_3 (
    .enable(enable), .reset(or_3_out), .run(enable), .a1(mod6_2_a), .reset_alarm(reset_alarm),
    .enable_alarm(enable_alarm), .buttonA(bamin), .a(mod10_3_a), .a10(mod10_3_a10), .display(out_18),
    .overflow_alarm(mod10_3_overflow_alarm));  // open: up0, button, b1, output1, b
  and and_8 (and_8_out, and_6_out, and_7_out);
  or or_3 (or_3_out, and_8_out, reset);
  mod6 mod6_2 (
    .enable(enable), .reset(or_3_out), .run(enable), .a1(mod10_4_a), .reset_alarm(reset_alarm),
    .enable_alarm(enable_alarm), .button(mod10_4_overflow_alarm), .a(mod6_2_a), .a6(mod6_2_a6),
    .display(out_16));  // open: up0, b1, output2, b
  or or_4 (or_4_out, weekdayinput, and_8_out);
  T_Flip_Flop t_ff_1 (.T(1'b1), .clk(or_4_out), .Q(wekdayout[0]), .Qn(t_ff_1_qn), .reset(and_10_out));  // open: preset
  mod10 mod10_4 (
    .enable(enable), .reset(or_3_out), .run(enable), .a1(clck), .reset_alarm(reset_alarm),
    .enable_alarm(enable_alarm), .buttonA(basec), .a(mod10_4_a), .a10(mod10_4_a10), .display(out_20),
    .overflow_alarm(mod10_4_overflow_alarm));  // open: up0, button, b1, output1, b
  T_Flip_Flop t_ff_2 (.T(1'b1), .clk(t_ff_1_qn), .Q(wekdayout[1]), .Qn(t_ff_2_qn), .reset(and_10_out));  // open: preset
  T_Flip_Flop t_ff_3 (.T(1'b1), .clk(t_ff_2_qn), .Q(wekdayout[2]), .reset(and_10_out));  // open: Qn, preset
  T_Flip_Flop t_ff_4 (.T(and_9_out), .clk(clock_1_out), .Q(t_ff_4_q), .reset(reset_alarm));  // open: Qn, preset
  and and_9 (and_9_out, mod3_2_a3, mod10_2_a10, mod6_1_a6, mod10_3_a10, mod6_2_a6, mod10_4_a10);
  Clock clock_1 (.out(clock_1_out));
  and and_10 (and_10_out, wekdayout[0], wekdayout[1], wekdayout[2]);
  T_Flip_Flop t_ff_5 (.T(t_ff_4_q), .clk(clock_2_out), .Q(t_ff_5_q), .reset(reset_alarm));  // open: Qn, preset
  Clock clock_2 (.out(clock_2_out));
  and and_11 (led, turnoff, t_ff_5_q);

  // Notes on the sheet:
  //   Here the reset is for 12 hours
  //   We will hijack the zeros in order to create a 12 hour clock
  //   The clock resets at 24 hours
  //   Yellow flashing led light will go off when the alarm is activated
  //   Weekday ripple counter
endmodule

module count (
  input  bhr,
  input  bmin,
  input  bsec,
  input  clck,
  input  up_down,
  input  enable,
  input  reset,
  input  run,
  output [3:0] out_9,
  output [3:0] out_10,
  output [3:0] out_11,
  output [3:0] out_12,
  output [3:0] out_13,
  output [3:0] out_14
);

  wire and_1_out, and_2_out, and_3_out, and_4_out, mod6_1_a, mod6_1_b, mod6_2_a, mod6_2_b, mod10_1_a,
       mod10_1_b, mod10_2_a, mod10_2_b, mod10_3_a, mod10_3_b, nand_1_out, nand_2_out, not_1_out, not_2_out,
       not_3_out, not_4_out, not_5_out, not_6_out;
  wire [3:0] and_5_out, mod6_1_display, mod6_2_display, mod10_3_display, not_7_out, not_8_out, not_9_out,
       not_10_out, not_11_out, not_12_out;

  and and_1 (and_1_out, and_5_out[3], and_5_out[2], and_5_out[1], and_5_out[0]);
  nand nand_1 (nand_1_out, and_1_out, up_down);
  not not_1 (not_1_out, out_14[0]);
  not not_2 (not_2_out, out_14[2]);
  not not_3 (not_3_out, out_14[3]);
  not not_4 (not_4_out, out_13[0]);
  not not_5 (not_5_out, out_13[1]);
  not not_6 (not_6_out, out_13[3]);
  and and_2 (and_2_out, not_1_out, out_14[1], not_2_out, not_3_out);
  and and_3 (and_3_out, not_4_out, not_5_out, out_13[2], not_6_out);
  and and_4 (and_4_out, enable, nand_1_out, nand_2_out);
  nand nand_2 (nand_2_out, and_2_out, and_3_out);
  mod3 mod3_1 (
    .up0(up_down), .enable(and_4_out), .reset(reset), .run(run), .a1(mod10_1_a), .b1(mod10_1_b),
    .output3(out_14));  // open: reset_alarm, enable_alarm, button, a, b, a3, display
  assign and_5_out = not_7_out & not_8_out & not_9_out & not_10_out & not_11_out & not_12_out;  // AND_Gate and_5, 4 bits wide
  assign not_7_out = ~out_12;  // NOT_Gate not_7, 4 bits wide
  assign not_8_out = ~out_11;  // NOT_Gate not_8, 4 bits wide
  assign not_9_out = ~out_9;  // NOT_Gate not_9, 4 bits wide
  assign not_10_out = ~out_10;  // NOT_Gate not_10, 4 bits wide
  assign not_11_out = ~out_13;  // NOT_Gate not_11, 4 bits wide
  assign not_12_out = ~out_14;  // NOT_Gate not_12, 4 bits wide
  mod10 mod10_1 (
    .up0(up_down), .enable(and_4_out), .reset(reset), .button(bhr), .run(run), .a1(mod6_1_a), .b1(mod6_1_b),
    .output1(out_13), .a(mod10_1_a), .b(mod10_1_b));  // open: reset_alarm, enable_alarm, buttonA, a10, display, overflow_alarm
  mod6 mod6_1 (
    .up0(up_down), .enable(and_4_out), .reset(reset), .run(run), .a1(mod10_2_a), .b1(mod10_2_b),
    .output2(out_10), .a(mod6_1_a), .b(mod6_1_b), .display(mod6_1_display));  // open: reset_alarm, enable_alarm, button, a6
  mod10 mod10_2 (
    .up0(up_down), .enable(and_4_out), .reset(reset), .button(bmin), .run(run), .a1(mod6_2_a), .b1(mod6_2_b),
    .output1(out_9), .a(mod10_2_a), .b(mod10_2_b));  // open: reset_alarm, enable_alarm, buttonA, a10, display, overflow_alarm
  mod6 mod6_2 (
    .up0(up_down), .enable(and_4_out), .reset(reset), .run(run), .a1(mod10_3_a), .b1(mod10_3_b),
    .output2(out_11), .a(mod6_2_a), .b(mod6_2_b), .display(mod6_2_display));  // open: reset_alarm, enable_alarm, button, a6
  mod10 mod10_3 (
    .up0(up_down), .enable(and_4_out), .reset(reset), .button(bsec), .run(run), .b1(clck), .output1(out_12),
    .a(mod10_3_a), .b(mod10_3_b), .display(mod10_3_display));  // open: a1, reset_alarm, enable_alarm, buttonA, a10, overflow_alarm

  // Notes on the sheet:
  //   Make sure that the stopwatch/timer automatically stops counting up at 24 hours and stops counting down at 0 hours
  //   Timer disables at 00:00:00
endmodule
